# Fritzing sketch die_roller (saved by Fritzing 0.7.12b)
breadboards: 1

parts:
  Arduino1 = Arduino
  U1 = 74HC595 [package="DIP16 [THT]"]
  R1 = Resistor [tolerance=±5% resistance=560 package=THT]
  R2 = Resistor [tolerance=±5% resistance=560 package=THT]
  R3 = Resistor [tolerance=±5% resistance=560 package=THT]
  R4 = Resistor [tolerance=±5% resistance=560 package=THT]
  R5 = Resistor [tolerance=±5% resistance=560 package=THT]
  R6 = Resistor [tolerance=±5% resistance=560 package=THT]
  LED1 = LED - 5mm [color="Red (633nm)" package="5 mm [THT]"]
  LED2 = LED - 5mm [color="Red (633nm)" package="5 mm [THT]"]
  LED3 = LED - 5mm [color="Red (633nm)" package="5 mm [THT]"]
  LED4 = LED - 5mm [color="Red (633nm)" package="5 mm [THT]"]
  LED5 = LED - 5mm [color="Red (633nm)" package="5 mm [THT]"]
  LED6 = LED - 5mm [color="Red (633nm)" package="5 mm [THT]"]
  LED7 = LED - 5mm [color="Red (633nm)" package="5 mm [THT]"]
  R7 = Resistor [tolerance=±5% resistance=560 package=THT]
  S1 = Pushbutton [package="[THT]"]

nets:
  GND: Arduino1.GND, U1.GND, U1.OE, LED1.cathode, LED2.cathode, LED3.cathode, LED4.cathode, LED5.cathode, LED6.cathode, LED7.cathode, S1.Pin_1, S1.Pin_2
  N1: Arduino1.D9, S1.Pin_3, S1.Pin_4
  N2: Arduino1.D6, U1.SH_CP
  N3: Arduino1.D5, U1.ST_CP
  N4: Arduino1.D4, U1.DS
  +5V: Arduino1.+5V, U1.MR, U1.VCC
  N5: U1.Q1, R4.Pin_1
  N6: U1.Q2, R5.Pin_1
  N7: U1.Q3, R1.Pin_1
  N8: U1.Q4, R2.Pin_1
  N9: U1.Q5, R7.Pin_1
  N10: U1.Q6, R3.Pin_1
  N11: U1.Q0, R6.Pin_1
  N12: R1.Pin_0, LED1.anode
  N13: R2.Pin_0, LED2.anode
  N14: R3.Pin_0, LED3.anode
  N15: R4.Pin_0, LED6.anode
  N16: R5.Pin_0, LED5.anode
  N17: R6.Pin_0, LED4.anode
  N18: LED7.anode, R7.Pin_0
